// Logisim project bilakhim.circ as structural Verilog
// HA
module Half_Adder (
  input  A,
  input  B,
  output S,
  output Cout
);

  xor xor_1 (S, A, B);
  and and_1 (Cout, A, B);
endmodule

// F A
module Full_Adder (
  input  A,
  input  B,
  input  Cin,
  output S,
  output Cout
);

  wire half_adder_1_cout, half_adder_1_s, half_adder_2_cout;

  Half_Adder half_adder_1 (.A(A), .B(B), .S(half_adder_1_s), .Cout(half_adder_1_cout));
  Half_Adder half_adder_2 (.A(half_adder_1_s), .B(Cin), .S(S), .Cout(half_adder_2_cout));
  or or_1 (Cout, half_adder_2_cout, half_adder_1_cout);
endmodule

module _2_MUX (
  input  A,
  input  B,
  input  Sel,
  output out
);

  wire and_1_out, and_2_out, not_1_out;

  not not_1 (not_1_out, Sel);
  and and_1 (and_1_out, A, not_1_out);
  and and_2 (and_2_out, B, Sel);
  xor xor_1 (out, and_1_out, and_2_out);
endmodule

// 4-mux
module _4_MUX (
  input  A,
  input  B,
  input  C,
  input  D,
  input  S0,
  input  S1,
  output out
);

  wire n2_mux_1_out, n2_mux_2_out;

  _2_MUX u_2_mux_1 (.A(A), .B(B), .Sel(S0), .out(n2_mux_1_out));
  _2_MUX u_2_mux_2 (.A(C), .B(D), .Sel(S0), .out(n2_mux_2_out));
  _2_MUX u_2_mux_3 (.A(n2_mux_1_out), .B(n2_mux_2_out), .Sel(S1), .out(out));
endmodule

module _1_Bit_ALU (
  input  A,
  input  B,
  input  Cin,
  input  Sel1,
  input  Sel0,
  output out,
  output Cout
);

  wire and_1_out, full_adder_1_s, or_1_out;

  and and_1 (and_1_out, A, B);
  or or_1 (or_1_out, A, B);
  Full_Adder full_adder_1 (.A(A), .B(B), .Cin(Cin), .S(full_adder_1_s), .Cout(Cout));
  _4_MUX u_4_mux_1 (
    .A(full_adder_1_s), .B(and_1_out), .C(or_1_out), .D(full_adder_1_s), .S1(Sel1), .S0(Sel0), .out(out));
endmodule

module _4_bit_Ripple (
  input  A0,
  input  B0,
  input  A1,
  input  B1,
  input  A2,
  input  B2,
  input  A3,
  input  B3,
  input  Sel1,
  input  Sel0,
  output S0,
  output S1,
  output S2,
  output S3,
  output Cout
);

  wire and_1_out, n1_bit_alu_1_cout, n1_bit_alu_2_cout, n1_bit_alu_3_cout;

  and and_1 (and_1_out, Sel0, Sel1);
  _1_Bit_ALU u_1_bit_alu_1 (
    .A(A0), .B(B0), .Cin(and_1_out), .Sel1(Sel1), .Sel0(Sel0), .out(S0), .Cout(n1_bit_alu_1_cout));
  _1_Bit_ALU u_1_bit_alu_2 (
    .A(A1), .B(B1), .Cin(n1_bit_alu_1_cout), .Sel1(Sel1), .Sel0(Sel0), .out(S1), .Cout(n1_bit_alu_2_cout));
  _1_Bit_ALU u_1_bit_alu_3 (
    .A(A2), .B(B2), .Cin(n1_bit_alu_2_cout), .Sel1(Sel1), .Sel0(Sel0), .out(S2), .Cout(n1_bit_alu_3_cout));
  _1_Bit_ALU u_1_bit_alu_4 (.A(A3), .B(B3), .Cin(n1_bit_alu_3_cout), .Sel1(Sel1), .Sel0(Sel0), .out(S3), .Cout(Cout));
endmodule

module Full_4_bit_ALU (
  input  A0,
  input  B0,
  input  A1,
  input  B1,
  input  A2,
  input  B2,
  input  A3,
  input  B3,
  input  Sel1,
  input  Sel0,
  output S0,
  output S1,
  output S3,
  output S4,
  output Cout,
  output X__Y
);

  wire and_1_out, and_2_out, and_3_out, n1_bit_alu_1_cout, n1_bit_alu_2_cout, n1_bit_alu_3_cout,
       n2_mux_1_out, n2_mux_2_out, n2_mux_3_out, n2_mux_4_out, not_1_out, not_2_out, not_3_out, not_4_out,
       not_5_out, or_1_out;

  not not_1 (not_1_out, B0);
  not not_2 (not_2_out, B1);
  not not_3 (not_3_out, B2);
  not not_4 (not_4_out, B3);
  and and_1 (and_1_out, Sel1, Sel0);
  _1_Bit_ALU u_1_bit_alu_1 (
    .A(A0), .B(n2_mux_1_out), .Cin(and_1_out), .Sel1(Sel1), .Sel0(Sel0), .out(S0), .Cout(n1_bit_alu_1_cout));
  _2_MUX u_2_mux_1 (.A(B0), .B(not_1_out), .Sel(and_1_out), .out(n2_mux_1_out));
  _2_MUX u_2_mux_2 (.A(B1), .B(not_2_out), .Sel(and_1_out), .out(n2_mux_2_out));
  _2_MUX u_2_mux_3 (.A(B2), .B(not_3_out), .Sel(and_1_out), .out(n2_mux_3_out));
  _2_MUX u_2_mux_4 (.A(B3), .B(not_4_out), .Sel(and_1_out), .out(n2_mux_4_out));
  _1_Bit_ALU u_1_bit_alu_2 (
    .A(A1), .B(n2_mux_2_out), .Cin(n1_bit_alu_1_cout), .Sel1(Sel1), .Sel0(Sel0), .out(S1),
    .Cout(n1_bit_alu_2_cout));
  _1_Bit_ALU u_1_bit_alu_3 (
    .A(A2), .B(n2_mux_3_out), .Cin(n1_bit_alu_2_cout), .Sel1(Sel1), .Sel0(Sel0), .out(S3),
    .Cout(n1_bit_alu_3_cout));
  _1_Bit_ALU u_1_bit_alu_4 (
    .A(A3), .B(n2_mux_4_out), .Cin(n1_bit_alu_3_cout), .Sel1(Sel1), .Sel0(Sel0), .out(S4), .Cout(Cout));
  and and_2 (and_2_out, Sel1, Sel0);
  or or_1 (or_1_out, S0, S1, S3, S4);
  not not_5 (not_5_out, or_1_out);
  and and_3 (and_3_out, not_5_out, and_2_out);
  or or_2 (X__Y, Cout, and_3_out);
endmodule
