// Logisim project 4-bit Register.circ as structural Verilog: 1 circuit, main circuit main
module main (
  input  Clock,
  input  [3:0] D_in,
  input  WE,
  output [3:0] out_4
);

  D_Flip_Flop d_ff_1 (.clk(Clock), .D(D_in[0]), .Q(out_4[0]), .en(WE));  // open: Qn, preset, reset
  D_Flip_Flop d_ff_2 (.clk(Clock), .D(D_in[1]), .Q(out_4[1]), .en(WE));  // open: Qn, preset, reset
  D_Flip_Flop d_ff_3 (.clk(Clock), .D(D_in[2]), .Q(out_4[2]), .en(WE));  // open: Qn, preset, reset
  D_Flip_Flop d_ff_4 (.clk(Clock), .D(D_in[3]), .Q(out_4[3]), .en(WE));  // open: Qn, preset, reset
endmodule
