// Logisim project bilakhim.circ as structural Verilog
// HA
module Half_Adder (
  input  A,
  input  B,
  output S,
  output Cout
);

  xor xor_1 (S, A, B);
  and and_1 (Cout, A, B);
endmodule

// F A
module Full_Adder (
  input  A,
  input  B,
  input  Cin,
  output S,
  output Cout
);

  wire half_adder_1_cout, half_adder_1_s, half_adder_2_cout;

  Half_Adder half_adder_1 (.A(A), .B(B), .S(half_adder_1_s), .Cout(half_adder_1_cout));
  Half_Adder half_adder_2 (.A(half_adder_1_s), .B(Cin), .S(S), .Cout(half_adder_2_cout));
  or or_1 (Cout, half_adder_2_cout, half_adder_1_cout);
endmodule

module _2_MUX (
  input  A,
  input  B,
  input  Sel,
  output out
);

  wire and_1_out, and_2_out, not_1_out;

  not not_1 (not_1_out, Sel);
  and and_1 (and_1_out, A, not_1_out);
  and and_2 (and_2_out, B, Sel);
  xor xor_1 (out, and_1_out, and_2_out);
endmodule

// 4-mux
module _4_MUX (
  input  A,
  input  B,
  input  C,
  input  D,
  input  S0,
  input  S1,
  output out
);

  wire n2_mux_1_out, n2_mux_2_out;

  _2_MUX u_2_mux_1 (.A(A), .B(B), .Sel(S0), .out(n2_mux_1_out));
  _2_MUX u_2_mux_2 (.A(C), .B(D), .Sel(S0), .out(n2_mux_2_out));
  _2_MUX u_2_mux_3 (.A(n2_mux_1_out), .B(n2_mux_2_out), .Sel(S1), .out(out));
endmodule

module _1_Bit_ALU (
  input  A,
  input  B,
  input  Cin,
  input  Sel1,
  input  Sel0,
  output out,
  output Cout
);

  wire and_1_out, full_adder_1_s, or_1_out;

  and and_1 (and_1_out, A, B);
  or or_1 (or_1_out, A, B);
  Full_Adder full_adder_1 (.A(A), .B(B), .Cin(Cin), .S(full_adder_1_s), .Cout(Cout));
  _4_MUX u_4_mux_1 (
    .A(full_adder_1_s), .B(and_1_out), .C(or_1_out), .D(full_adder_1_s), .S1(Sel1), .S0(Sel0), .out(out));
endmodule

module _4_bit_Ripple (
  input  A0,
  input  B0,
  input  A1,
  input  B1,
  input  A2,
  input  B2,
  input  A3,
  input  B3,
  input  Sel1,
  input  Sel0,
  output S0,
  output S1,
  output S2,
  output S3,
  output Cout
);

  wire and_1_out, n1_bit_alu_1_cout, n1_bit_alu_2_cout, n1_bit_alu_3_cout;

  and and_1 (and_1_out, Sel0, Sel1);
  _1_Bit_ALU u_1_bit_alu_1 (
    .A(A0), .B(B0), .Cin(and_1_out), .Sel1(Sel1), .Sel0(Sel0), .out(S0), .Cout(n1_bit_alu_1_cout));
  _1_Bit_ALU u_1_bit_alu_2 (
    .A(A1), .B(B1), .Cin(n1_bit_alu_1_cout), .Sel1(Sel1), .Sel0(Sel0), .out(S1), .Cout(n1_bit_alu_2_cout));
  _1_Bit_ALU u_1_bit_alu_3 (
    .A(A2), .B(B2), .Cin(n1_bit_alu_2_cout), .Sel1(Sel1), .Sel0(Sel0), .out(S2), .Cout(n1_bit_alu_3_cout));
  _1_Bit_ALU u_1_bit_alu_4 (.A(A3), .B(B3), .Cin(n1_bit_alu_3_cout), .Sel1(Sel1), .Sel0(Sel0), .out(S3), .Cout(Cout));
endmodule

module Full_4_bit_ALU (
  input  [3:0] A,
  input  [3:0] B,
  input  Sel1,
  input  Sel0,
  output S0,
  output S1,
  output S3,
  output S4,
  output Cout
);

  wire and_1_out, n1_bit_alu_1_cout, n1_bit_alu_2_cout, n1_bit_alu_3_cout, n2_mux_1_out, n2_mux_2_out,
       n2_mux_3_out, n2_mux_4_out, not_1_out, not_2_out, not_3_out, not_4_out;

  not not_1 (not_1_out, B[0]);
  and and_1 (and_1_out, Sel1, Sel0);
  _1_Bit_ALU u_1_bit_alu_1 (
    .A(A[0]), .B(n2_mux_1_out), .Cin(and_1_out), .Sel1(Sel1), .Sel0(Sel0), .out(S0), .Cout(n1_bit_alu_1_cout));
  _2_MUX u_2_mux_1 (.A(B[0]), .B(not_1_out), .Sel(and_1_out), .out(n2_mux_1_out));
  not not_2 (not_2_out, B[1]);
  _2_MUX u_2_mux_2 (.A(B[1]), .B(not_2_out), .Sel(and_1_out), .out(n2_mux_2_out));
  not not_3 (not_3_out, B[2]);
  _2_MUX u_2_mux_3 (.A(B[2]), .B(not_3_out), .Sel(and_1_out), .out(n2_mux_3_out));
  not not_4 (not_4_out, B[3]);
  _2_MUX u_2_mux_4 (.A(B[3]), .B(not_4_out), .Sel(and_1_out), .out(n2_mux_4_out));
  _1_Bit_ALU u_1_bit_alu_2 (
    .A(A[1]), .B(n2_mux_2_out), .Cin(n1_bit_alu_1_cout), .Sel1(Sel1), .Sel0(Sel0), .out(S1),
    .Cout(n1_bit_alu_2_cout));
  _1_Bit_ALU u_1_bit_alu_3 (
    .A(A[2]), .B(n2_mux_3_out), .Cin(n1_bit_alu_2_cout), .Sel1(Sel1), .Sel0(Sel0), .out(S3),
    .Cout(n1_bit_alu_3_cout));
  _1_Bit_ALU u_1_bit_alu_4 (
    .A(A[3]), .B(n2_mux_4_out), .Cin(n1_bit_alu_3_cout), .Sel1(Sel1), .Sel0(Sel0), .out(S4), .Cout(Cout));
endmodule

module _4_bit_register (
  input  Clock,
  input  [3:0] D_in,
  input  WE,
  output [3:0] out_4
);

  D_Flip_Flop d_ff_1 (.clk(Clock), .D(D_in[0]), .Q(out_4[0]), .en(WE));  // open: Qn, preset, reset
  D_Flip_Flop d_ff_2 (.clk(Clock), .D(D_in[1]), .Q(out_4[1]), .en(WE));  // open: Qn, preset, reset
  D_Flip_Flop d_ff_3 (.clk(Clock), .D(D_in[2]), .Q(out_4[2]), .en(WE));  // open: Qn, preset, reset
  D_Flip_Flop d_ff_4 (.clk(Clock), .D(D_in[3]), .Q(out_4[3]), .en(WE));  // open: Qn, preset, reset
endmodule

module Register_File (
  input  WE,
  input  [2:0] WA,
  input  clock,
  input  [3:0] D_in,
  input  [2:0] RA1,
  input  [2:0] RA2,
  output [3:0] out_7,
  output [3:0] out_8
);

  wire demultiplexer_1_out0, demultiplexer_1_out1, demultiplexer_1_out2, demultiplexer_1_out3,
       demultiplexer_1_out4, demultiplexer_1_out5, demultiplexer_1_out6, demultiplexer_1_out7;
  wire [3:0] n4_bit_register_1_out_4, n4_bit_register_2_out_4, n4_bit_register_3_out_4,
       n4_bit_register_4_out_4, n4_bit_register_5_out_4, n4_bit_register_6_out_4, n4_bit_register_7_out_4,
       n4_bit_register_8_out_4;

  Demultiplexer #(.select(3), .enable("false")) demultiplexer_1 (
    .out0(demultiplexer_1_out0), .out1(demultiplexer_1_out1), .out2(demultiplexer_1_out2),
    .out3(demultiplexer_1_out3), .out4(demultiplexer_1_out4), .out5(demultiplexer_1_out5),
    .out6(demultiplexer_1_out6), .out7(demultiplexer_1_out7), .in(WE), .sel(WA));
  _4_bit_register u_4_bit_register_1 (
    .Clock(clock), .D_in(D_in), .WE(demultiplexer_1_out7), .out_4(n4_bit_register_1_out_4));
  _4_bit_register u_4_bit_register_2 (
    .Clock(clock), .D_in(D_in), .WE(demultiplexer_1_out6), .out_4(n4_bit_register_2_out_4));
  _4_bit_register u_4_bit_register_3 (
    .Clock(clock), .D_in(D_in), .WE(demultiplexer_1_out5), .out_4(n4_bit_register_3_out_4));
  _4_bit_register u_4_bit_register_4 (
    .Clock(clock), .D_in(D_in), .WE(demultiplexer_1_out4), .out_4(n4_bit_register_4_out_4));
  _4_bit_register u_4_bit_register_5 (
    .Clock(clock), .D_in(D_in), .WE(demultiplexer_1_out3), .out_4(n4_bit_register_5_out_4));
  _4_bit_register u_4_bit_register_6 (
    .Clock(clock), .D_in(D_in), .WE(demultiplexer_1_out2), .out_4(n4_bit_register_6_out_4));
  _4_bit_register u_4_bit_register_7 (
    .Clock(clock), .D_in(D_in), .WE(demultiplexer_1_out1), .out_4(n4_bit_register_7_out_4));
  _4_bit_register u_4_bit_register_8 (
    .Clock(clock), .D_in(D_in), .WE(demultiplexer_1_out0), .out_4(n4_bit_register_8_out_4));
  Multiplexer #(.select(3), .width(4), .enable("false")) multiplexer_1 (
    .in0(n4_bit_register_8_out_4), .in1(n4_bit_register_7_out_4), .in2(n4_bit_register_6_out_4),
    .in3(n4_bit_register_5_out_4), .in4(n4_bit_register_4_out_4), .in5(n4_bit_register_3_out_4),
    .in6(n4_bit_register_2_out_4), .in7(n4_bit_register_1_out_4), .out(out_7), .sel(RA1));
  Multiplexer #(.select(3), .width(4), .enable("false")) multiplexer_2 (
    .in0(n4_bit_register_8_out_4), .in1(n4_bit_register_7_out_4), .in2(n4_bit_register_6_out_4),
    .in3(n4_bit_register_5_out_4), .in4(n4_bit_register_4_out_4), .in5(n4_bit_register_3_out_4),
    .in6(n4_bit_register_2_out_4), .in7(n4_bit_register_1_out_4), .out(out_8), .sel(RA2));
endmodule

module Register_file___ALU (
  input  WE,
  input  Clock,
  input  [11:0] I_OP_WA_RA1_RA2
);

  wire [3:0] bit_extender_1_out, full_4_bit_alu_1_s0, multiplexer_1_out, register_file_1_out_7,
       register_file_1_out_8;

  Multiplexer #(.width(4), .enable("false")) multiplexer_1 (
    .in0(register_file_1_out_8), .in1(bit_extender_1_out), .out(multiplexer_1_out), .sel(I_OP_WA_RA1_RA2[11]));
  assign bit_extender_1_out = {{1{1'b0}}, I_OP_WA_RA1_RA2[2:0]};  // Bit_Extender bit_extender_1
  Full_4_bit_ALU full_4_bit_alu_1 (
    .A(register_file_1_out_7), .B(multiplexer_1_out), .Sel1(I_OP_WA_RA1_RA2[10]), .Sel0(I_OP_WA_RA1_RA2[9]),
    .S0(full_4_bit_alu_1_s0[0]), .S1(full_4_bit_alu_1_s0[1]), .S3(full_4_bit_alu_1_s0[2]),
    .S4(full_4_bit_alu_1_s0[3]));  // open: Cout
  Register_File register_file_1 (
    .WE(WE), .WA(I_OP_WA_RA1_RA2[8:6]), .D_in(full_4_bit_alu_1_s0), .clock(Clock),
    .RA1(I_OP_WA_RA1_RA2[5:3]), .RA2(I_OP_WA_RA1_RA2[2:0]), .out_7(register_file_1_out_7),
    .out_8(register_file_1_out_8));
endmodule

module prelab4 (
  input  [3:0] in_1,
  output [11:0] out_2
);

  RAM #(.addrWidth(4), .dataWidth(12)) ram_1 (.addr(in_1), .data(out_2));  // open: sel, clk, ld, clr
endmodule
